# Fritzing sketch lueftung (saved by Fritzing 0.8.5b)
circuit board: 6.88566cm x 5.36311cm
breadboards: 2

parts:
  LCD1 = LCD screen
  R2 = Resistor [tolerance=±5% resistance=220 package=THT]
  Bauteil2 = Arduino Nano (Rev3.0)
  J1 = screw terminal, 2 pins [part_number="Power in"]
  J2 = screw terminal, 4 pins [part_number=VCC]
  J3 = screw terminal, 4 pins [part_number=GND]
  J4 = screw terminal, 4 pins [part_number=1W]
  R3 = Resistor [tolerance=±5% resistance=220 package=THT]
  Contrast1 = Trimmer Potentiometer [maximum_resistance=100kΩ package=THT]
  LED2 = LED - 3mm [color="Green (570nm)" package="3 mm [THT]"]
  LED1 = LED - 3mm [color="Red (633nm)" package="3 mm [THT]"]
  R4 = Resistor [tolerance=±5% resistance=220 package=THT]
  R5 = Resistor [tolerance=±5% resistance=220 package=THT]
  U1 = mystery part, 5 pins [chip_label=?]
  J5 = Piezo Speaker

nets:
  GND: LCD1.VSS, LCD1.R/W, LCD1.LED-, Bauteil2.GND, J1.pin2, J3.pin1, J3.pin2, J3.pin3, J3.pin4, Contrast1.leg1, U1.pin3, U1.pin5, J5.pin1
  5V: LCD1.VDD, R2.Pin_1, Bauteil2.5V, J2.pin1, J2.pin2, J2.pin3, J2.pin4, R3.Pin_0, Contrast1.leg2, LED2.anode, LED1.anode
  N1: LCD1.V0, Contrast1.wiper
  N2: LCD1.RS, Bauteil2.D12/MISO
  N3: LCD1.E, Bauteil2.D11/MOSI
  N4: LCD1.DB4, Bauteil2.D5
  N5: LCD1.DB5, Bauteil2.D4
  N6: LCD1.DB6, Bauteil2.D3
  N7: LCD1.DB7, Bauteil2.D2
  N8: LCD1.LED+, R2.Pin_0
  N9: Bauteil2.D6, J4.pin1, J4.pin2, J4.pin3, J4.pin4, R3.Pin_1
  N10: Bauteil2.VIN, J1.pin1
  N11: Bauteil2.A7, R4.Pin_0
  N12: Bauteil2.A6, R5.Pin_0
  N13: Bauteil2.A5, U1.pin1
  N14: Bauteil2.A4, U1.pin2
  N15: Bauteil2.A3, U1.pin4
  N16: Bauteil2.A2, J5.pin2
  N17: LED2.cathode, R5.Pin_1
  N18: LED1.cathode, R4.Pin_1
